# Fritzing sketch wiring (saved by Fritzing 0.9.3b)
breadboards: 1

parts:
  Part1 = Arduino Uno (Rev3) - ICSP
  Part2 = DHT22 module  # not connected
  Part3 = LC Studio SD Card Module

nets:
  N1: Part1.ICSP_MISO, Part1.D12/MISO, Part3.MISO
  N2: Part1.D10_PWM/SS, Part3.CS
  N3: Part1.D11_PWM/MOSI, Part3.MOSI
  N4: Part1.D13/SCK, Part3.SCK
  3V3: Part1.3V3, Part3.3V3
  GND: Part1.GND, Part3.GND

notes:
  Led1 on protoshield in DIGITAL PIN 8
  Led2 on protoshield in DIGITAL PIN 7
  Button on protoshield in DIGITAL PIN 1

custom parts:
  LC Studio SD Card Module: The LC Studio SD card module serves as an interface to an SD card. The module works at 3.3 volts and 5 volts. The SPI (Serial Peripheral Interface) protocol is used for communicating with the module.
